// Logisim project Basic boolean gates.circ as structural Verilog: 6 circuits, main circuit And_gate
module And_gate (
  input  a,
  input  b,
  output o
);

  wire nand_1_out;

  nand nand_1 (nand_1_out, a, b);
  nand nand_2 (o, nand_1_out, nand_1_out);
endmodule

module DMux_gate (
  input  sel,
  input  i,
  output a,
  output b
);

  wire not_1_out;

  not not_1 (not_1_out, sel);
  and and_1 (a, i, not_1_out);
  and and_2 (b, sel, i);
endmodule

module Mux_gate (
  input  sel,
  input  a,
  input  b,
  output o
);

  wire and_1_out, and_2_out, not_1_out;

  not not_1 (not_1_out, sel);
  and and_1 (and_1_out, not_1_out, a);
  and and_2 (and_2_out, sel, b);
  or or_1 (o, and_1_out, and_2_out);
endmodule

module Not_gate (
  input  i,
  output o
);

  nand nand_1 (o, i, i);
endmodule

module Or_gate (
  input  a,
  input  b,
  output o
);

  wire nand_1_out, nand_2_out;

  nand nand_1 (nand_1_out, a, a);
  nand nand_2 (nand_2_out, b, b);
  nand nand_3 (o, nand_1_out, nand_2_out);
endmodule

module Xor_gate (
  input  a,
  input  b,
  output o
);

  wire nand_1_out, nand_2_out, not_1_out, not_2_out;

  not not_1 (not_1_out, a);
  not not_2 (not_2_out, b);
  nand nand_1 (nand_1_out, a, not_2_out);
  nand nand_2 (nand_2_out, not_1_out, b);
  nand nand_3 (o, nand_1_out, nand_2_out);
endmodule
