// Logisim project Basic_logic_gates.circ as structural Verilog: 5 circuits, main circuit And_gate
module Not_gate (
  input  i,
  output o
);

  nand nand_1 (o, i, i);
endmodule

module And_gate (
  input  a,
  input  b,
  output o
);

  wire nand_1_out;

  nand nand_1 (nand_1_out, a, b);
  nand nand_2 (o, nand_1_out, nand_1_out);
endmodule

module Or_gate (
  input  a,
  input  b,
  output o
);

  wire nand_1_out, nand_2_out;

  nand nand_1 (nand_1_out, a, a);
  nand nand_2 (nand_2_out, b, b);
  nand nand_3 (o, nand_1_out, nand_2_out);
endmodule

module Xor_gate (
  input  a,
  input  b,
  output o
);

  wire nand_1_out, nand_2_out, not_1_out, not_2_out;

  not not_1 (not_1_out, a);
  not not_2 (not_2_out, b);
  nand nand_1 (nand_1_out, a, not_2_out);
  nand nand_2 (nand_2_out, not_1_out, b);
  nand nand_3 (o, nand_1_out, nand_2_out);
endmodule

module Nor_gate (
  input  a,
  input  b,
  output o
);

  wire nand_1_out, nand_2_out, nand_3_out;

  nand nand_1 (nand_1_out, a, a);
  nand nand_2 (nand_2_out, b, b);
  nand nand_3 (nand_3_out, nand_1_out, nand_2_out);
  nand nand_4 (o, nand_3_out, nand_3_out);
endmodule
