// Logisim project Mux_DMux.circ as structural Verilog: 2 circuits, main circuit Mux_gate
module Mux_gate (
  input  sel,
  input  a,
  input  b,
  output o
);

  wire and_1_out, and_2_out, not_1_out;

  not not_1 (not_1_out, sel);
  and and_1 (and_1_out, not_1_out, a);
  and and_2 (and_2_out, sel, b);
  or or_1 (o, and_1_out, and_2_out);
endmodule

module DMux_gate (
  input  sel,
  input  i,
  output a,
  output b
);

  wire not_1_out;

  not not_1 (not_1_out, sel);
  and and_1 (a, i, not_1_out);
  and and_2 (b, sel, i);
endmodule
