// Logisim project MWay_logic_gates.circ as structural Verilog: 3 circuits, main circuit DMux4Way
module DMux4Way (
  input  [1:0] sel,
  input  i,
  output a,
  output b,
  output c,
  output d
);

  wire demultiplexer_1_out0, demultiplexer_1_out1;

  Demultiplexer demultiplexer_1 (.out0(demultiplexer_1_out0), .out1(demultiplexer_1_out1), .in(i), .sel(sel[1]));
  Demultiplexer demultiplexer_2 (.out0(a), .out1(b), .in(demultiplexer_1_out0), .sel(sel[0]));
  Demultiplexer demultiplexer_3 (.out0(c), .out1(d), .in(demultiplexer_1_out1), .sel(sel[0]));
endmodule

module DMux8Way (
  input  [2:0] sel,
  input  i,
  output a,
  output b,
  output c,
  output d,
  output e,
  output f,
  output g,
  output h
);

  wire demultiplexer_1_out0, demultiplexer_1_out1, demultiplexer_2_out0, demultiplexer_2_out1,
       demultiplexer_3_out0, demultiplexer_3_out1;

  Demultiplexer demultiplexer_1 (
    .out0(demultiplexer_1_out0), .out1(demultiplexer_1_out1), .in(demultiplexer_2_out0), .sel(sel[1]));
  Demultiplexer demultiplexer_2 (.out0(demultiplexer_2_out0), .out1(demultiplexer_2_out1), .in(i), .sel(sel[2]));
  Demultiplexer demultiplexer_3 (
    .out0(demultiplexer_3_out0), .out1(demultiplexer_3_out1), .in(demultiplexer_2_out1), .sel(sel[1]));
  Demultiplexer demultiplexer_4 (.out0(a), .out1(b), .in(demultiplexer_1_out0), .sel(sel[0]));
  Demultiplexer demultiplexer_5 (.out0(c), .out1(d), .in(demultiplexer_1_out1), .sel(sel[0]));
  Demultiplexer demultiplexer_6 (.out0(e), .out1(f), .in(demultiplexer_3_out0), .sel(sel[0]));
  Demultiplexer demultiplexer_7 (.out0(g), .out1(h), .in(demultiplexer_3_out1), .sel(sel[0]));
endmodule

module Or8Way (
  input  [7:0] i,
  output o
);

  or or_1 (o, i[0], i[1], i[2], i[3], i[4], i[5], i[6], i[7]);
endmodule
