// Logisim project 16bit_logic_gates.circ as structural Verilog: 6 circuits, main circuit And16
module And16 (
  input  [15:0] a,
  input  [15:0] b,
  output [15:0] o
);

  assign o = a & b;  // AND_Gate and_1, 16 bits wide
endmodule

module Not16 (
  input  [15:0] i,
  output [15:0] o
);

  assign o = ~i;  // NOT_Gate not_1, 16 bits wide
endmodule

module Or16 (
  input  [15:0] a,
  input  [15:0] b,
  output [15:0] o
);

  assign o = a | b;  // OR_Gate or_1, 16 bits wide
endmodule

module Mux16 (
  input  [15:0] a,
  input  [15:0] b,
  input  sel,
  output [15:0] o
);

  Multiplexer #(.width(16)) multiplexer_1 (.in0(a), .in1(b), .out(o), .sel(sel));
endmodule

module Mux4Way16 (
  input  [15:0] a,
  input  [15:0] b,
  input  [15:0] c,
  input  [15:0] d,
  input  [1:0] sel,
  output [15:0] o
);

  Multiplexer #(.select(2), .width(16)) multiplexer_1 (.in0(a), .in1(b), .in2(c), .in3(d), .out(o), .sel(sel));
endmodule

module Mux8Way16 (
  input  [15:0] a,
  input  [15:0] b,
  input  [15:0] c,
  input  [15:0] d,
  input  [15:0] e,
  input  [15:0] f,
  input  [15:0] g,
  input  [15:0] h,
  input  [2:0] sel,
  output [15:0] o
);

  Multiplexer #(.select(3), .width(16)) multiplexer_1 (
    .in0(a), .in1(b), .in2(c), .in3(d), .in4(e), .in5(f), .in6(g), .in7(h), .out(o), .sel(sel));
endmodule
