// Logisim project Adder.circ as structural Verilog: 7 circuits, main circuit HalfAdder
module HalfAdder (
  input  a,
  input  b,
  output sum,
  output carry
);

  xor xor_1 (sum, a, b);
  and and_1 (carry, a, b);
endmodule

module FullAdder (
  input  a,
  input  b,
  input  c,
  output sum,
  output carry
);

  wire halfadder_1_carry, halfadder_1_sum, halfadder_2_carry;

  HalfAdder halfadder_1 (.a(a), .b(b), .sum(halfadder_1_sum), .carry(halfadder_1_carry));
  HalfAdder halfadder_2 (.a(halfadder_1_sum), .b(c), .sum(sum), .carry(halfadder_2_carry));
  or or_1 (carry, halfadder_2_carry, halfadder_1_carry);
endmodule

module Add2 (
  input  [1:0] a,
  input  [1:0] b,
  input  c,
  output [1:0] o,
  output carry
);

  wire fulladder_1_carry;

  FullAdder fulladder_1 (.a(a[0]), .b(b[0]), .c(c), .sum(o[0]), .carry(fulladder_1_carry));
  FullAdder fulladder_2 (.a(a[1]), .b(b[1]), .c(fulladder_1_carry), .sum(o[1]), .carry(carry));
endmodule

module Add4 (
  input  [3:0] a,
  input  [3:0] b,
  input  c,
  output [3:0] o,
  output carry
);

  wire add2_1_carry;

  Add2 add2_1 (.a(a[1:0]), .b(b[1:0]), .c(c), .o(o[1:0]), .carry(add2_1_carry));
  Add2 add2_2 (.a(a[3:2]), .b(b[3:2]), .c(add2_1_carry), .o(o[3:2]), .carry(carry));
endmodule

module Add8 (
  input  [7:0] a,
  input  [7:0] b,
  input  c,
  output [7:0] o,
  output carry
);

  wire add4_1_carry;

  Add4 add4_1 (.a(a[3:0]), .b(b[3:0]), .c(c), .o(o[3:0]), .carry(add4_1_carry));
  Add4 add4_2 (.a(a[7:4]), .b(b[7:4]), .c(add4_1_carry), .o(o[7:4]), .carry(carry));
endmodule

module Add16 (
  input  [15:0] a,
  input  [15:0] b,
  output [15:0] o
);

  wire add8_1_carry;

  Add8 add8_1 (.a(a[7:0]), .b(b[7:0]), .c(1'b0), .o(o[7:0]), .carry(add8_1_carry));
  Add8 add8_2 (.a(a[15:8]), .b(b[15:8]), .c(add8_1_carry), .o(o[15:8]));  // open: carry
endmodule

module Inc16 (
  input  [15:0] i,
  output [15:0] o
);

  Add16 add16_1 (.a(i), .b(16'h1), .o(o));
endmodule
