// Logisim project Memory.circ as structural Verilog: 3 circuits, main circuit bit
module \bit  (
  input  i,
  input  load,
  output o
);

  wire clock_1_out, multiplexer_1_out;

  Multiplexer multiplexer_1 (.in0(o), .in1(i), .out(multiplexer_1_out), .sel(load));
  Clock clock_1 (.out(clock_1_out));
  D_Flip_Flop d_ff_1 (.D(multiplexer_1_out), .clk(clock_1_out), .Q(o));  // open: Qn, preset, reset
endmodule

module PC (
  input  [15:0] i,
  input  load,
  input  inc,
  input  reset,
  output [15:0] out_5
);

  wire clock_1_out;
  wire [15:0] adder_1_out, multiplexer_1_out, multiplexer_2_out;

  Clock clock_1 (.out(clock_1_out));
  Multiplexer #(.width(16)) multiplexer_1 (.in0(multiplexer_2_out), .in1(i), .out(multiplexer_1_out), .sel(load));
  Register #(.width(16)) register_1 (.D(multiplexer_1_out), .clk(clock_1_out), .Q(out_5), .clr(reset));  // open: en
  Adder #(.width(16)) adder_1 (.a(16'h1), .b(out_5), .out(adder_1_out));  // open: cin, cout
  Multiplexer #(.width(16)) multiplexer_2 (.in0(out_5), .in1(adder_1_out), .out(multiplexer_2_out), .sel(inc));
endmodule

module RAM8 (
  input  [15:0] i,
  input  write,
  input  read,
  input  [2:0] address,
  output [15:0] out_5
);

  wire clock_1_out, demultiplexer_1_out0, demultiplexer_1_out1, demultiplexer_1_out2, demultiplexer_1_out3,
       demultiplexer_1_out4, demultiplexer_1_out5, demultiplexer_1_out6, demultiplexer_1_out7;
  wire [15:0] multiplexer_1_out, register_1_q, register_2_q, register_3_q, register_4_q, register_5_q,
       register_6_q, register_7_q, register_8_q;

  Clock clock_1 (.out(clock_1_out));
  Demultiplexer #(.select(3)) demultiplexer_1 (
    .out0(demultiplexer_1_out0), .out1(demultiplexer_1_out1), .out2(demultiplexer_1_out2),
    .out3(demultiplexer_1_out3), .out4(demultiplexer_1_out4), .out5(demultiplexer_1_out5),
    .out6(demultiplexer_1_out6), .out7(demultiplexer_1_out7), .in(write), .sel(address));
  Register #(.width(16)) register_1 (
    .D(i), .en(demultiplexer_1_out0), .clk(clock_1_out), .Q(register_1_q));  // open: clr
  Register #(.width(16)) register_2 (
    .D(i), .en(demultiplexer_1_out1), .clk(clock_1_out), .Q(register_2_q));  // open: clr
  Register #(.width(16)) register_3 (
    .D(i), .en(demultiplexer_1_out2), .clk(clock_1_out), .Q(register_3_q));  // open: clr
  Register #(.width(16)) register_4 (
    .D(i), .en(demultiplexer_1_out3), .clk(clock_1_out), .Q(register_4_q));  // open: clr
  Register #(.width(16)) register_5 (
    .D(i), .en(demultiplexer_1_out4), .clk(clock_1_out), .Q(register_5_q));  // open: clr
  Register #(.width(16)) register_6 (
    .D(i), .en(demultiplexer_1_out5), .clk(clock_1_out), .Q(register_6_q));  // open: clr
  Register #(.width(16)) register_7 (
    .D(i), .en(demultiplexer_1_out6), .clk(clock_1_out), .Q(register_7_q));  // open: clr
  Register #(.width(16)) register_8 (
    .D(i), .en(demultiplexer_1_out7), .clk(clock_1_out), .Q(register_8_q));  // open: clr
  Multiplexer #(.select(3), .width(16)) multiplexer_1 (
    .in0(register_1_q), .in1(register_2_q), .in2(register_3_q), .in3(register_4_q), .in4(register_5_q),
    .in5(register_6_q), .in6(register_7_q), .in7(register_8_q), .out(multiplexer_1_out), .sel(address));
  Multiplexer #(.width(16)) multiplexer_2 (.in0(16'haa55), .in1(multiplexer_1_out), .out(out_5), .sel(read));
endmodule
