// Logisim project Clock_Divider.circ as structural Verilog: 2 circuits, main circuit main
module main (
  output clk2,
  output clk1
);

  wire d_ff_1_q, d_ff_2_q, d_ff_3_q, d_ff_4_q, d_ff_5_q, d_ff_6_q, not_1_out;

  Clock clock_1 (.out(clk1));
  D_Flip_Flop d_ff_1 (.D(not_1_out), .clk(clk1), .Q(d_ff_1_q));  // open: Qn, preset, reset
  not not_1 (not_1_out, d_ff_6_q);
  D_Flip_Flop d_ff_2 (.D(d_ff_1_q), .clk(clk1), .Q(d_ff_2_q));  // open: Qn, preset, reset
  D_Flip_Flop d_ff_3 (.D(d_ff_2_q), .clk(clk1), .Q(d_ff_3_q));  // open: Qn, preset, reset
  D_Flip_Flop d_ff_4 (.D(d_ff_3_q), .clk(clk1), .Q(d_ff_4_q));  // open: Qn, preset, reset
  // Digital_Oscilloscope #(.nState(29)) digital_oscilloscope_1: pin names not known; wires that end beside it: clk1, clk1, clk2
  D_Flip_Flop d_ff_5 (.D(d_ff_4_q), .clk(clk1), .Q(d_ff_5_q));  // open: Qn, preset, reset
  D_Flip_Flop d_ff_6 (.D(d_ff_5_q), .clk(clk1), .Q(d_ff_6_q), .Qn(clk2));  // open: preset, reset
endmodule

module test (
  input  [3:0] in_1,
  input  [3:0] in_2
);

  wire main_1_clk1, main_1_clk2;
  wire [6:0] random_1_out, rgb_video_1_p3, rgb_video_1_p4, rgb_video_2_p4;

  main main_1 (.clk2(main_1_clk2), .clk1(main_1_clk1));
  Random #(.width(7)) random_1 (.next(1'b1), .clk(main_1_clk1), .out(random_1_out));  // open: clr
  // RGB_Video rgb_video_1: pin names not known; wires that end beside it: main_1_clk2, 1'b1, rgb_video_1_p3, rgb_video_1_p4, in_1
  // RGB_Video rgb_video_2: pin names not known; wires that end beside it: main_1_clk1, 1'b1, random_1_out, rgb_video_2_p4, in_2
  Random #(.width(7)) random_2 (.next(1'b1), .clk(main_1_clk1), .out(rgb_video_2_p4));  // open: clr
  Random #(.width(7)) random_3 (.next(1'b1), .clk(main_1_clk2), .out(rgb_video_1_p3));  // open: clr
  Random #(.width(7)) random_4 (.next(1'b1), .clk(main_1_clk2), .out(rgb_video_1_p4));  // open: clr
endmodule
