// Logisim project Hack_computer.circ as structural Verilog
module Hack_Computer (
  input  reset,
  input  debug_instruction,
  output [14:0] out_3,
  output [15:0] out_4,
  output out_5,
  output [14:0] out_6,
  output [15:0] out_7,
  output [15:0] out_8,
  output [6:0] out_9
);

  wire clock_divider_1_clk2, CPU_clk, read_KBD, rgb_video_1_p2, video_clk, video_driver_1_w_screen2, w_screen;
  wire [3:0] rgb_video_1_p5, video_driver_1_color2;
  wire [7:0] rgb_video_1_p3, rgb_video_1_p4, video_driver_1_x2, video_driver_1_y2;
  wire [12:0] addr_screen;

  RAM #(.addrWidth(15), .dataWidth(16), .\type ("nonvolatile")) ram_1 (
    .addr(out_3), .oe(1'b1), .clk(CPU_clk), .dout(out_4));  // open: we, din
  Keyboard #(.buflen(10)) keyboard_1 (.clk(CPU_clk), .re(read_KBD), .data(out_9));  // open: clr, avail
  clock_divider clock_divider_1 (.clk1(video_clk), .clk2(clock_divider_1_clk2));
  Multiplexer multiplexer_1 (.in0(clock_divider_1_clk2), .in1(video_clk), .out(CPU_clk), .sel(debug_instruction));
  CPU cpu_1 (
    .instruction(out_4), .D_in_M(out_8), .clk(CPU_clk), .reset(reset), .P_C(out_3), .w_M(out_5),
    .D_out_M(out_7), .addr_M(out_6));
  Memory memory_1 (
    .address(out_6), .write(out_5), .D_in(out_7), .D_KBD_in(out_9), .clk(CPU_clk), .D_out(out_8),
    .w_screen(w_screen), .addr_screen(addr_screen), .read_KBD(read_KBD));
  // RGB_Video #(.cursor("No Cursor"), .height(256), .reset("Synchronous"), .scale(3), .width(256)) rgb_video_1: pin names not known; wires that end beside it: video_clk, rgb_video_1_p2, rgb_video_1_p3, rgb_video_1_p4, rgb_video_1_p5
  video_driver video_driver_1 (
    .v_clock(video_clk), .v_enable(w_screen), .v_address(addr_screen), .vram_in(out_7),
    .w_screen1(rgb_video_1_p2), .w_screen2(video_driver_1_w_screen2), .x1(rgb_video_1_p3),
    .x2(video_driver_1_x2), .y1(rgb_video_1_p4), .y2(video_driver_1_y2), .color1(rgb_video_1_p5),
    .color2(video_driver_1_color2));
  // RGB_Video #(.cursor("No Cursor"), .height(256), .reset("Synchronous"), .scale(3), .width(256)) rgb_video_2: pin names not known; wires that end beside it: video_clk, video_driver_1_w_screen2, video_driver_1_x2, video_driver_1_y2, video_driver_1_color2

  // Other names for the same wires on the sheet: addr_M[14:0] = out_6; D_in_M[15:0] = out_7; D_out_KBD[6:0] = out_9;
  //   D_out_M[15:0] = out_8; instruction[15:0] = out_4; PC[14:0] = out_3; w_M = out_5
endmodule

module clock_divider (
  output clk1,
  output clk2
);

  wire d_ff_1_q, d_ff_2_q, d_ff_3_q, d_ff_4_q, d_ff_5_q, d_ff_6_q, d_ff_7_q, not_1_out;

  Clock clock_1 (.out(clk1));
  D_Flip_Flop d_ff_1 (.D(not_1_out), .clk(clk1), .Q(d_ff_1_q));  // open: Qn, preset, reset
  not not_1 (not_1_out, clk2);
  D_Flip_Flop d_ff_2 (.D(d_ff_1_q), .clk(clk1), .Q(d_ff_2_q));  // open: Qn, preset, reset
  // Digital_Oscilloscope #(.nState(20)) digital_oscilloscope_1: pin names not known; wires that end beside it: clk1, clk1, clk2
  D_Flip_Flop d_ff_3 (.D(d_ff_2_q), .clk(clk1), .Q(d_ff_3_q));  // open: Qn, preset, reset
  D_Flip_Flop d_ff_4 (.D(d_ff_3_q), .clk(clk1), .Q(d_ff_4_q));  // open: Qn, preset, reset
  D_Flip_Flop d_ff_5 (.D(d_ff_4_q), .clk(clk1), .Q(d_ff_5_q));  // open: Qn, preset, reset
  D_Flip_Flop d_ff_6 (.D(d_ff_5_q), .clk(clk1), .Q(d_ff_6_q));  // open: Qn, preset, reset
  D_Flip_Flop d_ff_7 (.D(d_ff_6_q), .clk(clk1), .Q(d_ff_7_q));  // open: Qn, preset, reset
  D_Flip_Flop d_ff_8 (.D(d_ff_7_q), .clk(clk1), .Q(clk2));  // open: Qn, preset, reset
endmodule

module video_driver (
  input  v_clock,
  input  v_enable,
  input  [12:0] v_address,
  input  [15:0] vram_in,
  output w_screen1,
  output w_screen2,
  output [7:0] x1,
  output [7:0] x2,
  output [7:0] y1,
  output [7:0] y2,
  output [3:0] color1,
  output [3:0] color2
);

  wire multiplexer_1_out, not_1_out;
  wire [3:0] counter_1_q;

  Counter #(.max('hf), .width(4)) counter_1 (.clk(v_clock), .Q(counter_1_q));  // open: clr, load, up, count, D, carry
  Multiplexer #(.select(4)) multiplexer_1 (
    .in0(vram_in[0]), .in1(vram_in[1]), .in2(vram_in[2]), .in3(vram_in[3]), .in4(vram_in[4]),
    .in5(vram_in[5]), .in6(vram_in[6]), .in7(vram_in[7]), .in8(vram_in[8]), .in9(vram_in[9]),
    .in10(vram_in[10]), .in11(vram_in[11]), .in12(vram_in[12]), .in13(vram_in[13]), .in14(vram_in[14]),
    .in15(vram_in[15]), .out(multiplexer_1_out), .sel(counter_1_q));
  not not_1 (not_1_out, v_address[4]);
  Demultiplexer #(.width(8)) demultiplexer_1 (
    .out0(x1), .out1(x2), .in({v_address[3:0], counter_1_q}), .sel(v_address[4]));
  Demultiplexer #(.width(8)) demultiplexer_2 (.out0(y1), .out1(y2), .in(v_address[12:5]), .sel(v_address[4]));
  and and_1 (w_screen1, v_enable, not_1_out);
  and and_2 (w_screen2, v_enable, v_address[4]);
  Multiplexer #(.width(4)) multiplexer_2 (.in0(4'b1111), .in1(4'b0000), .out(color1), .sel(multiplexer_1_out));

  assign color2 = color1;
endmodule

module video_driver_test (
  output [3:0] out_1
);

  wire clock_divider_1_clk1, clock_divider_1_clk2, multiplexer_1_out, not_1_out;
  wire [3:0] rgb_video_1_p5;
  wire [7:0] demultiplexer_1_out1, demultiplexer_2_out1, rgb_video_1_p3, rgb_video_1_p4;
  wire [12:0] counter_1_q;
  wire [15:0] ram_1_dout;

  Counter #(.max('h1fff), .width(13)) counter_1 (
    .clk(clock_divider_1_clk2), .Q(counter_1_q));  // open: clr, load, up, count, D, carry
  RAM #(.addrWidth(13), .dataWidth(16)) ram_1 (
    .addr(counter_1_q), .we(1'b1), .oe(1'b1), .clk(clock_divider_1_clk2), .din({16{1'b1}}), .dout(ram_1_dout));
  clock_divider clock_divider_1 (.clk1(clock_divider_1_clk1), .clk2(clock_divider_1_clk2));
  Counter #(.max('hf), .width(4)) counter_2 (
    .clk(clock_divider_1_clk1), .Q(out_1));  // open: clr, load, up, count, D, carry
  not not_1 (not_1_out, counter_1_q[4]);
  Multiplexer #(.select(4)) multiplexer_1 (
    .in0(ram_1_dout[0]), .in1(ram_1_dout[1]), .in2(ram_1_dout[2]), .in3(ram_1_dout[3]), .in4(ram_1_dout[4]),
    .in5(ram_1_dout[5]), .in6(ram_1_dout[6]), .in7(ram_1_dout[7]), .in8(ram_1_dout[8]), .in9(ram_1_dout[9]),
    .in10(ram_1_dout[10]), .in11(ram_1_dout[11]), .in12(ram_1_dout[12]), .in13(ram_1_dout[13]),
    .in14(ram_1_dout[14]), .in15(ram_1_dout[15]), .out(multiplexer_1_out), .sel(out_1));
  // RGB_Video #(.cursor("No Cursor"), .height(256), .reset("Synchronous"), .scale(1), .width(256)) rgb_video_1: pin names not known; wires that end beside it: clock_divider_1_clk1, not_1_out, rgb_video_1_p3, rgb_video_1_p4, rgb_video_1_p5
  Demultiplexer #(.width(8)) demultiplexer_1 (
    .out0(rgb_video_1_p4), .out1(demultiplexer_1_out1), .in(counter_1_q[12:5]), .sel(counter_1_q[4]));
  Demultiplexer #(.width(8)) demultiplexer_2 (
    .out0(rgb_video_1_p3), .out1(demultiplexer_2_out1), .in({counter_1_q[3:0], out_1}), .sel(counter_1_q[4]));
  Multiplexer #(.width(4)) multiplexer_2 (.in0(4'b1111), .in1(4'b0000), .out(rgb_video_1_p5), .sel(multiplexer_1_out));
  // RGB_Video #(.cursor("No Cursor"), .height(256), .reset("Synchronous"), .scale(1), .width(256)) rgb_video_2: pin names not known; wires that end beside it: clock_divider_1_clk1, counter_1_q[4], demultiplexer_2_out1, demultiplexer_1_out1, rgb_video_1_p5
endmodule

module CPU (
  input  [15:0] instruction,
  input  [15:0] D_in_M,
  input  clk,
  input  reset,
  output [14:0] P_C,
  output w_M,
  output [15:0] D_out_M,
  output [14:0] addr_M
);

  wire A_instr, and_7_out, and_8_out, and_9_out, compM, Dest_A, Dest_D, jeq, jgt, jlt, neg, not_1_out,
       or_3_out, or_4_out, PC_inc, PC_load, pos, zero;
  wire [15:0] ALUOut, D, multiplexer_1_out, multiplexer_2_out;
  wire [15:15] A, pc_1_out_6;

  and and_1 (w_M, instruction[3], instruction[15]);
  and and_2 (Dest_D, instruction[4], instruction[15]);
  and and_3 (Dest_A, instruction[5], instruction[15]);
  and and_4 (jgt, instruction[0], instruction[15]);
  and and_5 (jeq, instruction[1], instruction[15]);
  and and_6 (jlt, instruction[2], instruction[15]);
  and and_7 (and_7_out, zero, jeq);
  and and_8 (and_8_out, neg, jlt);
  and and_9 (and_9_out, pos, jgt);
  and and_10 (compM, instruction[12], instruction[15]);
  or or_1 (PC_load, and_7_out, and_8_out, and_9_out);
  not not_1 (not_1_out, PC_load);
  or or_2 (PC_inc, A_instr, not_1_out);
  Multiplexer #(.width(16)) multiplexer_1 (.in0({A[15], addr_M}), .in1(D_in_M), .out(multiplexer_1_out), .sel(compM));
  not not_2 (A_instr, instruction[15]);
  Register #(.width(16)) register_1 (.D(ALUOut), .en(Dest_D), .clk(clk), .Q(D), .clr(reset));
  PC pc_1 (.i({A[15], addr_M}), .load(PC_load), .inc(PC_inc), .clk(clk), .reset(reset), .out_6({pc_1_out_6[15], P_C}));
  Multiplexer #(.width(16)) multiplexer_2 (.in0(ALUOut), .in1(instruction), .out(multiplexer_2_out), .sel(A_instr));
  or or_3 (or_3_out, A_instr, Dest_A);
  ALU alu_1 (
    .x(D), .zx(instruction[11]), .nx(instruction[10]), .y(multiplexer_1_out), .zy(instruction[9]),
    .ny(instruction[8]), .f(instruction[7]), .no(instruction[6]), .o(ALUOut), .zr(zero), .ng(neg));
  Register #(.width(16)) register_2 (.D(multiplexer_2_out), .en(or_3_out), .clk(clk), .Q({A[15], addr_M}), .clr(reset));
  or or_4 (or_4_out, zero, neg);
  not not_3 (pos, or_4_out);
  Multiplexer #(.width(16)) multiplexer_3 (.in0({16{1'b0}}), .in1(ALUOut), .out(D_out_M), .sel(w_M));

  // Other names for the same wires on the sheet: A[14:0] = addr_M; CPU_clk = clk; CPU_reset = reset; Dest_M = w_M;
  //   instr[15:0] = instruction; JMP_ctrl[2:0] = instruction[2:0]; Dest_ctrl[2:0] = instruction[5:3];
  //   ALU_ctrl[5:0] = instruction[11:6]; C_instr = instruction[15]
endmodule

module ALU (
  input  [15:0] x,
  input  zx,
  input  nx,
  input  [15:0] y,
  input  zy,
  input  ny,
  input  f,
  input  no,
  output [15:0] o,
  output zr,
  output ng
);

  wire or_1_out;
  wire [15:0] adder_1_out, and_1_out, multiplexer_1_out, multiplexer_2_out, multiplexer_3_out,
       multiplexer_4_out, multiplexer_5_out, not_1_out, not_2_out, not_3_out;

  Multiplexer #(.width(16)) multiplexer_1 (.in0(x), .in1({16{1'b0}}), .out(multiplexer_1_out), .sel(zx));
  Multiplexer #(.width(16)) multiplexer_2 (.in0(y), .in1({16{1'b0}}), .out(multiplexer_2_out), .sel(zy));
  Multiplexer #(.width(16)) multiplexer_3 (.in0(multiplexer_1_out), .in1(not_1_out), .out(multiplexer_3_out), .sel(nx));
  assign not_1_out = ~multiplexer_1_out;  // NOT_Gate not_1, 16 bits wide
  Multiplexer #(.width(16)) multiplexer_4 (.in0(multiplexer_2_out), .in1(not_2_out), .out(multiplexer_4_out), .sel(ny));
  assign not_2_out = ~multiplexer_2_out;  // NOT_Gate not_2, 16 bits wide
  assign and_1_out = multiplexer_3_out & multiplexer_4_out;  // AND_Gate and_1, 16 bits wide
  Adder #(.width(16)) adder_1 (.a(multiplexer_3_out), .b(multiplexer_4_out), .out(adder_1_out));  // open: cin, cout
  Multiplexer #(.width(16)) multiplexer_5 (.in0(and_1_out), .in1(adder_1_out), .out(multiplexer_5_out), .sel(f));
  assign not_3_out = ~multiplexer_5_out;  // NOT_Gate not_3, 16 bits wide
  Multiplexer #(.width(16)) multiplexer_6 (.in0(multiplexer_5_out), .in1(not_3_out), .out({ng, o[14:0]}), .sel(no));
  or or_1 (or_1_out, o[0], o[1], o[2], o[3], o[4], o[5], o[6], o[7], o[8], o[9], o[10], o[11], o[12], o[13], o[14], ng);
  not not_4 (zr, or_1_out);

  assign o[15] = ng;
endmodule

module PC (
  input  [15:0] i,
  input  load,
  input  inc,
  input  clk,
  input  reset,
  output [15:0] out_6
);

  wire [15:0] adder_1_out, multiplexer_1_out, multiplexer_2_out;

  Multiplexer #(.width(16)) multiplexer_1 (.in0(multiplexer_2_out), .in1(i), .out(multiplexer_1_out), .sel(load));
  Register #(.width(16)) register_1 (.D(multiplexer_1_out), .clk(clk), .Q(out_6), .clr(reset));  // open: en
  Adder #(.width(16)) adder_1 (.a(16'h1), .b(out_6), .out(adder_1_out));  // open: cin, cout
  Multiplexer #(.width(16)) multiplexer_2 (.in0(out_6), .in1(adder_1_out), .out(multiplexer_2_out), .sel(inc));
endmodule

module Memory (
  input  [14:0] address,
  input  write,
  input  [15:0] D_in,
  input  [6:0] D_KBD_in,
  input  clk,
  output [15:0] D_out,
  output w_screen,
  output [12:0] addr_screen,
  output read_KBD
);

  wire d_ff_1_q, demultiplexer_1_out1, sel_RAM, w_RAM;
  wire [15:0] D_RAM, D_screen, multiplexer_1_out;

  not not_1 (sel_RAM, address[14]);
  Demultiplexer demultiplexer_1 (.out0(w_RAM), .out1(demultiplexer_1_out1), .in(write), .sel(address[14]));
  Demultiplexer demultiplexer_2 (.out0(w_screen), .in(demultiplexer_1_out1), .sel(address[13]));  // open: out1
  RAM #(.addrWidth(14), .asyncread("true"), .dataWidth(16)) ram_1 (
    .addr(address[13:0]), .we(w_RAM), .oe(sel_RAM), .clk(clk), .din(D_in), .dout(D_RAM));
  RAM #(.addrWidth(13), .asyncread("true"), .dataWidth(16)) ram_2 (
    .addr(address[12:0]), .we(w_screen), .oe(address[14]), .clk(clk), .din(D_in), .dout(D_screen));
  D_Flip_Flop d_ff_1 (.D(address[13]), .clk(clk), .Q(d_ff_1_q));  // open: Qn, preset, reset
  Multiplexer #(.width(16)) multiplexer_1 (.in0(D_RAM), .in1(D_screen), .out(multiplexer_1_out), .sel(address[14]));
  Multiplexer #(.width(16)) multiplexer_2 (
    .in0(multiplexer_1_out), .in1({{9{1'b0}}, D_KBD_in}), .out(D_out), .sel(address[13]));
  and and_1 (read_KBD, address[13], d_ff_1_q);

  assign addr_screen = address[12:0];

  // Other names for the same wires on the sheet: addr_RAM[13:0] = address[13:0]; sel_KBD = address[13];
  //   sel_screen = address[14]; D_KBD[6:0] = D_KBD_in
endmodule
