// Logisim project VRAM.circ as structural Verilog: 9 circuits, main circuit VRAM_t1
module Wire_reverse16 (
  input  [15:0] in_1,
  output [15:0] out_2
);


  assign out_2 = {in_1[0], in_1[1], in_1[2], in_1[3], in_1[4], in_1[5], in_1[6], in_1[7], in_1[8], in_1[9], in_1[10], in_1[11], in_1[12], in_1[13], in_1[14], in_1[15]};
endmodule

module VRAM_t1 (
  input  [7:0] in_1
);

  wire clock_1_out;
  wire [7:0] register_1_q, register_2_q, register_3_q, register_4_q;

  Clock clock_1 (.out(clock_1_out));
  Register register_1 (.D(in_1), .en(1'b1), .clk(clock_1_out), .Q(register_1_q));  // open: clr
  Register register_2 (.D(in_1), .en(1'b1), .clk(clock_1_out), .Q(register_2_q));  // open: clr
  Register register_3 (.D(in_1), .en(1'b1), .clk(clock_1_out), .Q(register_3_q));  // open: clr
  Register register_4 (.D(in_1), .en(1'b1), .clk(clock_1_out), .Q(register_4_q));  // open: clr
  DotMatrix #(.inputtype("row"), .matrixcols(16), .matrixrows(2)) dotmatrix_1 (
    .row0({register_2_q, register_1_q}), .row1({register_4_q, register_3_q}));
endmodule

module VRAM_4_64p (
  input  venable,
  input  [1:0] sel,
  input  clk,
  input  [15:0] vin,
  output [63:0] vout
);

  wire demultiplexer_2_out0, demultiplexer_2_out1, demultiplexer_2_out2, demultiplexer_2_out3;
  wire [15:0] demultiplexer_1_out0, demultiplexer_1_out1, demultiplexer_1_out2, demultiplexer_1_out3,
       ram_1_dout, register_1_q, register_2_q, register_3_q, register_4_q;

  RAM #(.addrWidth(2), .dataWidth(16), .enables("line")) ram_1 (
    .addr(sel), .we(1'b1), .clk(clk), .din(vin), .dout(ram_1_dout));
  Demultiplexer #(.select(2), .width(16)) demultiplexer_1 (
    .out0(demultiplexer_1_out0), .out1(demultiplexer_1_out1), .out2(demultiplexer_1_out2),
    .out3(demultiplexer_1_out3), .in(ram_1_dout), .sel(sel));
  Demultiplexer #(.select(2)) demultiplexer_2 (
    .out0(demultiplexer_2_out0), .out1(demultiplexer_2_out1), .out2(demultiplexer_2_out2),
    .out3(demultiplexer_2_out3), .in(venable), .sel(sel));
  Register #(.width(16)) register_1 (
    .D(demultiplexer_1_out0), .en(demultiplexer_2_out0), .clk(clk), .Q(register_1_q));  // open: clr
  Register #(.width(16)) register_2 (
    .D(demultiplexer_1_out1), .en(demultiplexer_2_out1), .clk(clk), .Q(register_2_q));  // open: clr
  Register #(.width(16)) register_3 (
    .D(demultiplexer_1_out2), .en(demultiplexer_2_out2), .clk(clk), .Q(register_3_q));  // open: clr
  Register #(.width(16)) register_4 (
    .D(demultiplexer_1_out3), .en(demultiplexer_2_out3), .clk(clk), .Q(register_4_q));  // open: clr
  Wire_reverse16 wire_reverse16_1 (.in_1(register_1_q), .out_2(vout[63:48]));
  Wire_reverse16 wire_reverse16_2 (.in_1(register_2_q), .out_2(vout[47:32]));
  Wire_reverse16 wire_reverse16_3 (.in_1(register_3_q), .out_2(vout[31:16]));
  Wire_reverse16 wire_reverse16_4 (.in_1(register_4_q), .out_2(vout[15:0]));
endmodule

module VRAM_8_128p (
  input  venable,
  input  [2:0] sel,
  input  clk,
  input  [15:0] vin,
  output [63:0] vout1,
  output [63:0] vout2
);

  wire demultiplexer_1_out0, demultiplexer_1_out1;
  wire [1:0] demultiplexer_2_out0, demultiplexer_2_out1;

  Demultiplexer demultiplexer_1 (.out0(demultiplexer_1_out0), .out1(demultiplexer_1_out1), .in(venable), .sel(sel[2]));
  Demultiplexer #(.width(2)) demultiplexer_2 (
    .out0(demultiplexer_2_out0), .out1(demultiplexer_2_out1), .in(sel[1:0]), .sel(sel[2]));
  VRAM_4_64p vram_4_64p_1 (
    .venable(demultiplexer_1_out0), .sel(demultiplexer_2_out0), .clk(clk), .vin(vin), .vout(vout1));
  VRAM_4_64p vram_4_64p_2 (
    .venable(demultiplexer_1_out1), .sel(demultiplexer_2_out1), .clk(clk), .vin(vin), .vout(vout2));
endmodule

module VRAM_16_256p (
  input  venable,
  input  [3:0] sel,
  input  clk,
  input  [15:0] vin,
  output [63:0] vout1,
  output [63:0] vout2,
  output [63:0] vout3,
  output [63:0] vout4
);

  wire demultiplexer_1_out0, demultiplexer_1_out1;
  wire [2:0] demultiplexer_2_out0, demultiplexer_2_out1;

  Demultiplexer demultiplexer_1 (.out0(demultiplexer_1_out0), .out1(demultiplexer_1_out1), .in(venable), .sel(sel[3]));
  Demultiplexer #(.width(3)) demultiplexer_2 (
    .out0(demultiplexer_2_out0), .out1(demultiplexer_2_out1), .in(sel[2:0]), .sel(sel[3]));
  VRAM_8_128p vram_8_128p_1 (
    .venable(demultiplexer_1_out0), .sel(demultiplexer_2_out0), .clk(clk), .vin(vin), .vout1(vout1),
    .vout2(vout2));
  VRAM_8_128p vram_8_128p_2 (
    .venable(demultiplexer_1_out1), .sel(demultiplexer_2_out1), .clk(clk), .vin(vin), .vout1(vout3),
    .vout2(vout4));
endmodule

module VRAM_32_512p (
  input  venable,
  input  [4:0] sel,
  input  clk,
  input  [15:0] vin,
  output [63:0] col16_1,
  output [63:0] col16_2,
  output [63:0] col16_3,
  output [63:0] col16_4,
  output [63:0] col16_5,
  output [63:0] col16_6,
  output [63:0] col16_7,
  output [63:0] col16_8
);

  wire demultiplexer_1_out0, demultiplexer_1_out1;
  wire [3:0] demultiplexer_2_out0, demultiplexer_2_out1;

  Demultiplexer demultiplexer_1 (.out0(demultiplexer_1_out0), .out1(demultiplexer_1_out1), .in(venable), .sel(sel[4]));
  Demultiplexer #(.width(4)) demultiplexer_2 (
    .out0(demultiplexer_2_out0), .out1(demultiplexer_2_out1), .in(sel[3:0]), .sel(sel[4]));
  VRAM_16_256p vram_16_256p_1 (
    .venable(demultiplexer_1_out0), .sel(demultiplexer_2_out0), .clk(clk), .vin(vin), .vout1(col16_1),
    .vout2(col16_2), .vout3(col16_3), .vout4(col16_4));
  VRAM_16_256p vram_16_256p_2 (
    .venable(demultiplexer_1_out1), .sel(demultiplexer_2_out1), .clk(clk), .vin(vin), .vout1(col16_5),
    .vout2(col16_6), .vout3(col16_7), .vout4(col16_8));
  DotMatrix #(.inputtype("row"), .matrixcols(64), .matrixrows(1)) dotmatrix_1 ();  // open: row0
endmodule

module VRAM_32_512p_2r (
  input  venable,
  input  [5:0] sel,
  input  clk,
  input  [15:0] vin,
  output [63:0] r1_c1,
  output [63:0] r1_c2,
  output [63:0] r1_c3,
  output [63:0] r1_c4,
  output [63:0] r1_c5,
  output [63:0] r1_c6,
  output [63:0] r1_c7,
  output [63:0] r1_c8,
  output [63:0] r2_c1,
  output [63:0] r2_c2,
  output [63:0] r2_c3,
  output [63:0] r2_c4,
  output [63:0] r2_c5,
  output [63:0] r2_c6,
  output [63:0] r2_c7,
  output [63:0] r2_c8
);

  wire demultiplexer_1_out0, demultiplexer_1_out1;
  wire [4:0] demultiplexer_2_out0, demultiplexer_2_out1;

  Demultiplexer demultiplexer_1 (.out0(demultiplexer_1_out0), .out1(demultiplexer_1_out1), .in(venable), .sel(sel[5]));
  Demultiplexer #(.width(5)) demultiplexer_2 (
    .out0(demultiplexer_2_out0), .out1(demultiplexer_2_out1), .in(sel[4:0]), .sel(sel[5]));
  VRAM_32_512p vram_32_512p_1 (
    .venable(demultiplexer_1_out0), .sel(demultiplexer_2_out0), .clk(clk), .vin(vin), .col16_1(r1_c1),
    .col16_2(r1_c2), .col16_3(r1_c3), .col16_4(r1_c4), .col16_5(r1_c5), .col16_6(r1_c6), .col16_7(r1_c7),
    .col16_8(r1_c8));
  VRAM_32_512p vram_32_512p_2 (
    .venable(demultiplexer_1_out1), .sel(demultiplexer_2_out1), .clk(clk), .vin(vin), .col16_1(r2_c1),
    .col16_2(r2_c2), .col16_3(r2_c3), .col16_4(r2_c4), .col16_5(r2_c5), .col16_6(r2_c6), .col16_7(r2_c7),
    .col16_8(r2_c8));
  DotMatrix #(.inputtype("row"), .matrixcols(64), .matrixrows(1)) dotmatrix_1 ();  // open: row0
endmodule

module VRAM_32_521p_4r (
  input  venable,
  input  [6:0] sel,
  input  clk,
  input  [15:0] vin,
  output [63:0] r1_c1,
  output [63:0] r1_c2,
  output [63:0] r1_c3,
  output [63:0] r1_c5,
  output [63:0] r1_c4,
  output [63:0] r1_c6,
  output [63:0] r1_c7,
  output [63:0] r1_c8,
  output [63:0] r2_c1,
  output [63:0] r2_c2,
  output [63:0] r2_c3,
  output [63:0] r2_c5,
  output [63:0] r2_c4,
  output [63:0] r2_c6,
  output [63:0] r2_c7,
  output [63:0] r2_c8,
  output [63:0] r3_c1,
  output [63:0] r3_c2,
  output [63:0] r3_c3,
  output [63:0] r3_c5,
  output [63:0] r3_c4,
  output [63:0] r3_c6,
  output [63:0] r3_c7,
  output [63:0] r3_c8,
  output [63:0] r4_c1,
  output [63:0] r4_c2,
  output [63:0] r4_c3,
  output [63:0] r4_c5,
  output [63:0] r4_c4,
  output [63:0] r4_c6,
  output [63:0] r4_c7,
  output [63:0] r4_c8
);

  wire demultiplexer_1_out0, demultiplexer_1_out1;
  wire [5:0] demultiplexer_2_out0, demultiplexer_2_out1;

  DotMatrix #(.inputtype("row"), .matrixcols(64), .matrixrows(1)) dotmatrix_1 ();  // open: row0
  Demultiplexer demultiplexer_1 (.out0(demultiplexer_1_out0), .out1(demultiplexer_1_out1), .in(venable), .sel(sel[6]));
  Demultiplexer #(.width(6)) demultiplexer_2 (
    .out0(demultiplexer_2_out0), .out1(demultiplexer_2_out1), .in(sel[5:0]), .sel(sel[6]));
  VRAM_32_512p_2r vram_32_512p_2r_1 (
    .venable(demultiplexer_1_out0), .sel(demultiplexer_2_out0), .clk(clk), .vin(vin), .r1_c1(r1_c1),
    .r1_c2(r1_c2), .r1_c3(r1_c3), .r1_c4(r1_c4), .r1_c5(r1_c5), .r1_c6(r1_c6), .r1_c7(r1_c7), .r1_c8(r1_c8),
    .r2_c1(r2_c1), .r2_c2(r2_c2), .r2_c3(r2_c3), .r2_c4(r2_c4), .r2_c5(r2_c5), .r2_c6(r2_c6), .r2_c7(r2_c7),
    .r2_c8(r2_c8));
  VRAM_32_512p_2r vram_32_512p_2r_2 (
    .venable(demultiplexer_1_out1), .sel(demultiplexer_2_out1), .clk(clk), .vin(vin), .r1_c1(r3_c1),
    .r1_c2(r3_c2), .r1_c3(r3_c3), .r1_c4(r3_c4), .r1_c5(r3_c5), .r1_c6(r3_c6), .r1_c7(r3_c7), .r1_c8(r3_c8),
    .r2_c1(r4_c1), .r2_c2(r4_c2), .r2_c3(r4_c3), .r2_c4(r4_c4), .r2_c5(r4_c5), .r2_c6(r4_c6), .r2_c7(r4_c7),
    .r2_c8(r4_c8));
endmodule

module VRAM_driver_test (
  input  [3:0] in_1
);

  wire clock_1_out;
  wire [7:0] demultiplexer_1_out1, demultiplexer_1_out1_2;
  wire [15:0] demultiplexer_1_out0;
  wire [16:0] counter_1_q;

  Counter #(.max('h1ffff), .width(17)) counter_1 (
    .clk(clock_1_out), .Q(counter_1_q));  // open: clr, load, up, count, D, carry
  Clock clock_1 (.out(clock_1_out));
  Demultiplexer #(.width(16)) demultiplexer_1 (
    .out0(demultiplexer_1_out0), .out1({demultiplexer_1_out1_2, demultiplexer_1_out1}),
    .in(counter_1_q[16:1]), .sel(counter_1_q[0]));
  // RGB_Video #(.cursor("No Cursor"), .height(256), .scale(1), .width(256)) rgb_video_1: pin names not known; wires that end beside it: 1'b1, clock_1_out, 1'b1, demultiplexer_1_out0[7:0], demultiplexer_1_out0[15:8], in_1
  // RGB_Video #(.cursor("No Cursor"), .height(256), .scale(1), .width(256)) rgb_video_2: pin names not known; wires that end beside it: clock_1_out, 1'b1, demultiplexer_1_out1, demultiplexer_1_out1_2, in_1
endmodule
